// Logisim project BreadboardComputer.circ as structural Verilog: 1 circuit, main circuit main
module main (
);

  wire clock_1_out;

  Clock clock_1 (.out(clock_1_out));
  // RGBLED rgbled_1: pin names not known; wires that end beside it: clock_1_out, clock_1_out, clock_1_out
endmodule
